# Fritzing sketch RC (saved by Fritzing 0.9.3b)

parts:
  Raspberry_Pi_1 = Raspberry Pi 3 [part_number=RPI-3-V1.2]
  L298N1 = L298N DC motor driver
  LED1 = LED - 5mm [color="Red (633nm)" package="5 mm [THT]"]
  LED2 = LED - 5mm [color="Red (633nm)" package="5 mm [THT]"]
  LED3 = LED - 5mm [color="White (8000K)" package="5 mm [THT]"]  # not connected
  LED4 = LED - 5mm [color="White (8000K)" package="5 mm [THT]"]
  M2 = DC Motor
  J1 = Piezo Speaker
  M1 = DC Motor
  hc-sr1 = hc-sr04

nets:
  N1: Raspberry_Pi_1.GIPO4, J1.pin2
  GND: Raspberry_Pi_1.GND, LED2.cathode, LED4.cathode, J1.pin1, hc-sr1.GND
  N2: Raspberry_Pi_1.GIPO17, L298N1.5V#9, L298N1.ENA
  N3: Raspberry_Pi_1.GIPO27, L298N1.IN1
  N4: Raspberry_Pi_1.GIPO22, L298N1.IN2
  N5: Raspberry_Pi_1.GIPO10, L298N1.IN3
  N6: Raspberry_Pi_1.GIPO9, L298N1.IN4
  N7: Raspberry_Pi_1.GIPO11, L298N1.5V#10, L298N1.ENB
  N8: Raspberry_Pi_1.GIPO5, LED4.anode
  N9: Raspberry_Pi_1.GIPO6, LED1.cathode, LED2.anode
  N10: Raspberry_Pi_1.GIPO7, hc-sr1.Trig
  N11: Raspberry_Pi_1.GIPO8, hc-sr1.Echo
  5V: Raspberry_Pi_1.5V, hc-sr1.VCC
  N12: L298N1.OUT1, M2.pin_1
  N13: L298N1.OUT2, M2.pin_2
  N14: L298N1.OUT3, M1.pin_1
  N15: L298N1.OUT4, M1.pin_2

custom parts:
  L298N DC motor driver: 2x DC motor driver with 78M05 positive voltage regulator (7..35 V) L298N: max 46 V, 2 A Set 5 V Enable jumper to enable 5 V regultor (needed for the L298N) and +5 V output at screw terminal or supply external +5 V at screw terminal Set ENA and/or ENB to +5 V to enable motor permanently or supply ENA and/or ENB with PWM signal IN1 and IN2 set rotation directory for motor A (OUT1/OUT2) IN2 and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
